# Fritzing sketch esp32_slave (saved by Fritzing 0.9.6b)

parts:
  U1 = keyestudio ESP32 plus development board [part_number=ESP32]
  RFM95W_2 = RFM95W LoRa Modul  # not connected
  IC1 = KS0034 [chip_label=?]
  IC2 = KS0028 [chip_label=?]
  PIR1 = KS0052 PIR sensor
  Componente1 = Adafruit MAX4466 Electret Microphone Amplifier [part_number="Adafruit #1063"]

nets:
  N1: U1.io25, PIR1.S
  N2: U1.io17, IC1.S
  N3: U1.io34, IC2.S
  GND: U1.GND, IC1.GND, IC2.GND, PIR1.GND, Componente1.GND
  VCC: U1.VCC, IC1.VCC, IC2.VCC, PIR1.VCC, Componente1.VCC
  N4: U1.io2, Componente1.OUT

custom parts:
  keyestudio ESP32 plus development board: keyestudio ESP32 plus STEM makers development board 2.4GHz dual-mode WiFi + bluetooth dual cores microcontroller
  RFM95W LoRa Modul: Modulo LoRa de InnovaDidactic para uso con ArduinoBlocks www.arduinoblocks.com
  KS0034: DHT-11
  KS0028: LDR
  KS0052 PIR sensor: PIR sensor
  Adafruit MAX4466 Electret Microphone Amplifier: Add an ear to your project with this well-designed electret microphone amplifier. This fully assembled and tested board comes with a 20-20KHz electret microphone soldered on. For the amplification, we use the Maxim MAX4466, an op-amp specifically designed for this delicate task! The amplifier has excellent power supply noise rejection, so this amplifier sounds really good and isn't nearly as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
