# Fritzing sketch nodo_smartplace (saved by Fritzing 0.9.6b)

parts:
  U1 = keyestudio ESP32 plus development board [part_number=ESP32]
  DHT22 = KS0034 [chip_label=?]
  LDR = KS0028 [chip_label=?]
  Micrófono = Adafruit MAX4466 Electret Microphone Amplifier [part_number="Adafruit #1063"]
  CO2 = Adafruit CCS811 [part_number="Adafruit #3566"]
  Sensor_Partículas = Adafruit PMSA003I Air Quality Breakout [part_number="Adafruit #4632"]
  RFM95W_1 = RFM95W LoRa Modul  # not connected
  RGB = KS0032 [chip_label=?]

nets:
  N1: U1.io26, DHT22.S
  N2: U1.io25, RGB.B
  N3: U1.io17, RGB.R
  N4: U1.io16, RGB.G
  N5: U1.io4, Micrófono.OUT
  GND: U1.GND, DHT22.GND, LDR.GND, Micrófono.GND, CO2.GND, Sensor_Partículas.GND
  VCC: U1.5V, U1.VCC, DHT22.VCC, LDR.VCC, Micrófono.VCC, CO2.VCC, Sensor_Partículas.VCC, RGB.VCC
  N6: U1.SDA, CO2.SDA, Sensor_Partículas.SDA
  N7: U1.SCL, CO2.SCL, Sensor_Partículas.SCL
  N8: U1.io2, LDR.S

custom parts:
  keyestudio ESP32 plus development board: keyestudio ESP32 plus STEM makers development board 2.4GHz dual-mode WiFi + bluetooth dual cores microcontroller
  KS0034: DHT-11
  KS0028: LDR
  Adafruit MAX4466 Electret Microphone Amplifier: Add an ear to your project with this well-designed electret microphone amplifier. This fully assembled and tested board comes with a 20-20KHz electret microphone soldered on. For the amplification, we use the Maxim MAX4466, an op-amp specifically designed for this delicate task! The amplifier has excellent power supply noise rejection, so this amplifier sounds really good and isn't nearly as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
  Adafruit CCS811: Breathe easy - we finally have an I2C VOC/eCO2 sensor in the Adafruit shop! Add air quality monitoring to your project and with an Adafruit CCS811 Air Quality Sensor Breakout. This sensor from AMS is a gas sensor that can detect a wide range of Volatile Organic Compounds (VOCs) and is intended for indoor air quality monitoring. When connected to your microcontroller (running our library code)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
  Adafruit PMSA003I Air Quality Breakout: Breathe easy, knowing that you can track and sense the quality of the air around you with this Adafruit PMSA003I Air Quality Breakout. This sensor is great for monitoring air quality, in a compact plug-in format. Best of all, unlike almost all other sensors we've seen that are UART interface, this one is I2C interface, which makes it a great match for single board Linux computers like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
  RFM95W LoRa Modul: Modulo LoRa de InnovaDidactic para uso con ArduinoBlocks www.arduinoblocks.com
  KS0032: RGB Led (common anode)
